// Logisim project alu.circ as structural Verilog: 1 circuit, main circuit main
module main (
  input  [31:0] X,
  input  [31:0] Y,
  input  [5:0] Switch__S,
  input  [5:0] in_4,
  output Signed_Overflow,
  output [31:0] RESULT,
  output Equal
);

  wire and_2_out, comparator_1_eq, comparator_1_gt, comparator_2_lt, comparator_3_lt, comparator_5_lt,
       comparator_6_lt, comparator_7_lt, comparator_8_eq, even_parity_1_out;
  wire [4:0] bit_extender_1_out;
  wire [31:0] adder_1_out, adder_2_out, and_1_out, bit_extender_2_out, bit_extender_3_out,
       bit_extender_4_out, multiplexer_1_out, or_1_out, shifter_1_out, shifter_2_out, shifter_3_out,
       subtractor_1_out, subtractor_2_out, undriven;

  // Probe on X
  // Probe on Y
  Bit_Extender #(.in_width(32), .out_width(5)) bit_extender_1 (.in(Y), .out(bit_extender_1_out));
  Comparator #(.width(6)) comparator_1 (
    .a(Switch__S), .b(in_4), .gt(comparator_1_gt), .eq(comparator_1_eq));  // open: lt
  // Probe on comparator_2_lt
  Comparator #(.width(32)) comparator_2 (.a(Y), .b({32{1'b0}}), .lt(comparator_2_lt));  // open: gt, eq
  Comparator #(.width(32)) comparator_3 (.a(X), .b({32{1'b0}}), .lt(comparator_3_lt));  // open: gt, eq
  // Probe on comparator_3_lt
  xnor even_parity_1 (even_parity_1_out, comparator_1_gt, comparator_1_eq);
  Comparator #(.width(32)) comparator_4 (.a(Y), .b(X), .eq(Equal));  // open: gt, lt
  Shifter #(.width(32)) shifter_1 (.in(X), .\dist (bit_extender_1_out), .out(shifter_1_out));
  Shifter #(.width(32), .shift("lr")) shifter_2 (.in(X), .\dist (bit_extender_1_out), .out(shifter_2_out));
  Shifter #(.width(32), .shift("ar")) shifter_3 (.in(X), .\dist (bit_extender_1_out), .out(shifter_3_out));
  Adder #(.width(32)) adder_1 (.a(X), .b(Y), .out(adder_1_out));  // open: cin, cout
  Adder #(.width(32)) adder_2 (.a(X), .b(Y), .out(adder_2_out));  // open: cin, cout
  Subtractor #(.width(32)) subtractor_1 (.a(X), .b(Y), .out(subtractor_1_out));  // open: bin, bout
  Subtractor #(.width(32)) subtractor_2 (.a(X), .b(Y), .out(subtractor_2_out));  // open: bin, bout
  assign and_1_out = X & Y;  // AND_Gate and_1, 32 bits wide
  assign or_1_out = X | Y;  // OR_Gate or_1, 32 bits wide
  Comparator #(.width(32)) comparator_5 (.a(X), .b(Y), .lt(comparator_5_lt));  // open: gt, eq
  Comparator #(.width(32), .mode("unsigned")) comparator_6 (.a(X), .b(Y), .lt(comparator_6_lt));  // open: gt, eq
  // Probe on and_2_out
  and and_2 (and_2_out, comparator_2_lt, comparator_3_lt);
  assign bit_extender_2_out = {{31{1'b0}}, comparator_5_lt};  // Bit_Extender bit_extender_2
  assign bit_extender_3_out = {{31{1'b0}}, comparator_6_lt};  // Bit_Extender bit_extender_3
  Multiplexer #(.width(32), .enable("false")) multiplexer_1 (
    .in0(adder_1_out), .in1(subtractor_1_out), .out(multiplexer_1_out), .sel(even_parity_1_out));
  // Probe on comparator_7_lt
  Comparator #(.width(32)) comparator_7 (.a(multiplexer_1_out), .b({32{1'b0}}), .lt(comparator_7_lt));  // open: gt, eq
  // Probe on and_2_out
  // Probe on multiplexer_1_out
  assign bit_extender_4_out = {{31{1'b0}}, comparator_8_eq};  // Bit_Extender bit_extender_4
  xor xor_1 (Signed_Overflow, comparator_7_lt, and_2_out);
  Multiplexer #(.select(5), .width(32), .enable("false")) multiplexer_2 (
    .in0(shifter_1_out), .in2(shifter_2_out), .in3(shifter_3_out), .in16(adder_1_out), .in17(adder_2_out),
    .in18(subtractor_1_out), .in19(subtractor_2_out), .in20(and_1_out), .in21(or_1_out),
    .in26(bit_extender_2_out), .in27(bit_extender_3_out), .in30(bit_extender_4_out), .in31(undriven),
    .out(RESULT), .sel({Switch__S[5], Switch__S[3:0]}));  // open: in1, in4, in5, in6, in7, in8, in9, in10, in11, in12, in13, in14, in15, in22, in23, in24, in25, in28, in29
  // Probe on Signed_Overflow
  Comparator #(.width(16)) comparator_8 (.a(X[31:16]), .b(X[15:0]), .eq(comparator_8_eq));  // open: gt, lt

  // Notes on the sheet:
  //   INPUTS to your circuit
  //   INPUT to your circuit
  //   DON'T CHANGE THE INPUTS AND OUTPUTS! IF YOU DO SO, YOU NEED TO MAKE SURE THE PINS ARE IN THE RIGHT PLACES!
  //   OUTPUTS of your circuit
endmodule
